# Fritzing sketch receiver (saved by Fritzing 0.9.3b)
circuit board: 6.49209cm x 5.35493cm

parts:
  NodeMCU = NodeMCU V1.0
  IR_Receiver = KY-022 Infrared Receiver Module [package="Breakout board"]

nets:
  3V3: NodeMCU.3V3, IR_Receiver.Vin
  N1: NodeMCU.GND, IR_Receiver.-
  N2: NodeMCU.D5, IR_Receiver.S

custom parts:
  NodeMCU V1.0: ESP8266 based NodeMCU
  KY-022 Infrared Receiver Module: Arduino IR receiver module KY-022, based on 1838 IR Receiver/Decoder. It reacts to 38kHz infrared light.
