# Fritzing sketch transmitter (saved by Fritzing 0.9.3b)
circuit board: 8.46667cm x 5.64444cm

parts:
  NodeMCU1 = NodeMCU V1.0
  IR_Transmitter = KY-005 Infrared Transmitter Module [package="Breakout board"]

nets:
  3V3: NodeMCU1.3V3, IR_Transmitter.Vin
  N1: NodeMCU1.GND, IR_Transmitter.-
  N2: NodeMCU1.D5, IR_Transmitter.S

custom parts:
  NodeMCU V1.0: ESP8266 based NodeMCU
  KY-005 Infrared Transmitter Module: Arduino IR Transmitter Module Keyes KY-005, emits infrared light at 38KHz.
